# Fritzing sketch esquema (saved by Fritzing 0.9.6b)
breadboards: 1

parts:
  TD-er1 = MH-Z19 CO2 sensor [part_number=MH-Z19]
  WeMos_D1_Mini1 = WeMos D1 Mini
  RHT1 = Humidity and Temperature Sensor RHT03

nets:
  N1: TD-er1.RX, WeMos_D1_Mini1.RX
  N2: TD-er1.TX, WeMos_D1_Mini1.TX
  VIN: TD-er1.Vin, WeMos_D1_Mini1.5V, RHT1.Vcc
  N3: TD-er1.GND, WeMos_D1_Mini1.G, RHT1.GND_1
  N4: WeMos_D1_Mini1.D4, RHT1.Data-signal
